// Logisim project DIVS4XS4.circ as structural Verilog: 5 circuits, main circuit main
module main (
  input  [3:0] dividend,
  input  D3,
  input  D2,
  input  D1,
  input  D0,
  input  d03,
  input  d02,
  input  d01,
  input  d00,
  input  [3:0] divisor,
  input  opsigned,
  output eover,
  output ediv0,
  output [3:0] remainder,
  output [3:0] quotient,
  output [3:0] out_16,
  output [3:0] out_17,
  output [3:0] out_18,
  output [3:0] out_19,
  output [3:0] out_20,
  output [3:0] out_21,
  output [3:0] out_22,
  output [3:0] out_23
);

  wire and_1_out, and_2_out, clock_1_out, comparator_3_eq, comparator_4_eq, counter_1_carry, DUQ0D0d0_c,
       DUQ0D0d0_s, DUQ0D0d1_c, DUQ0D0d1_s, DUQ0D0d2_c, DUQ0D0d2_s, DUQ0D0d3_c, DUQ0D0d3_s, DUQ0D0d4_EXT_s,
       DUQ1D1d0_c, DUQ1D1d0_s, DUQ1D1d1_c, DUQ1D1d1_s, DUQ1D1d2_c, DUQ1D1d2_s, DUQ1D1d3_c, DUQ1D1d3_s,
       DUQ1D1d4_EXT_s, DUQ2D2d0_c, DUQ2D2d0_s, DUQ2D2d1_c, DUQ2D2d1_s, DUQ2D2d2_c, DUQ2D2d2_s, DUQ2D2d3_s,
       DUQ3D3d0_c, DUQ3D3d0_s, DUQ3D3d01_c, DUQ3D3d01_s, DUQ3D3d2_c, DUQ3D3d2_s, DVD_TWOS_EN_out,
       DVR_TWOS_EN_out, HAD0_DVD_TWOS_c, HAD0_DVD_TWOS_s, HAD1_DVD_TWOS_c, HAD1_DVD_TWOS_s, HAD2_DVD_TWOS_c,
       HAD2_DVD_TWOS_s, HAD3_DVD_TWOS_c, HAD3_DVD_TWOS_s, HAQ0_SIGN_c, HAQ1_SIGN_c, HAQ2_SIGN_c, HAQ3_SIGN_c,
       HAR0_SIGN_c, HAR1_SIGN_c, HAR2_SIGN_c, HAR3_SIGN_c, not_1_out, or_1_out, QSIGN, RESET_out, XDIV0,
       XOR_Q0_SIGN_out, XOR_Q1_SIGN_out, XOR_Q2_SIGN_out, XOR_Q3_SIGN_out, XOR_R0_SIGN_out, XOR_R1_SIGN_out,
       XOR_R2_SIGN_out, XOR_R3_SIGN_out, XORD0_DVD_TWOS_out, XORD0_DVR_out, XORD1_DVD_TWOS_out,
       XORD1_DVR_out, XORD2_DVD_TWOS_out, XORD2_DVR_out, XORD3_DVD_TWOS_out, XORD3_DVR_out, XQ, XR;
  wire [3:0] DUQ0D0d4_EXT_c, Q, R;
  wire [7:0] counter_1_q;

  Clock clock_1 (.out(clock_1_out));
  // Digital_Oscilloscope #(.nState(32)) digital_oscilloscope_1: pin names not known; wires that end beside it: clock_1_out, out_22[0], out_22[1], out_22[2], out_22[3], out_20[0], out_20[1], out_20[2], out_20[3], Q[0], Q[1]
  Button RESET (.out(RESET_out));
  xor XORD0_DVD_TWOS (XORD0_DVD_TWOS_out, out_22[0], DVD_TWOS_EN_out);
  and DVD_TWOS_EN (DVD_TWOS_EN_out, out_22[3], opsigned);
  and DVR_TWOS_EN (DVR_TWOS_EN_out, opsigned, out_20[3]);
  and DIV0ERROR (ediv0, ~out_20[3], ~out_20[2], ~out_20[1], ~out_20[0]);  // AND_Gate
  Counter counter_1 (
    .clr(RESET_out), .load(1'b0), .up(1'b1), .count(1'b1), .clk(clock_1_out), .D({8{1'b0}}),
    .carry(counter_1_carry), .Q(counter_1_q));
  xor xor_1 (QSIGN, DVD_TWOS_EN_out, DVR_TWOS_EN_out);
  not not_1 (not_1_out, DVR_TWOS_EN_out);
  HA HAD0_DVD_TWOS (.A(XORD0_DVD_TWOS_out), .B(DVD_TWOS_EN_out), .C(HAD0_DVD_TWOS_c), .S(HAD0_DVD_TWOS_s));
  xor XOR_R0_SIGN (XOR_R0_SIGN_out, DUQ0D0d0_s, DVD_TWOS_EN_out);
  ROM #(.dataWidth(16)) rom_1 (.addr(counter_1_q), .data({out_22, out_20, out_18, out_16}));
  xor XORD1_DVD_TWOS (XORD1_DVD_TWOS_out, out_22[1], DVD_TWOS_EN_out);
  xor XORD3_DVR (XORD3_DVR_out, out_20[3], not_1_out);
  xor XORD2_DVR (XORD2_DVR_out, out_20[2], not_1_out);
  xor XORD1_DVR (XORD1_DVR_out, out_20[1], not_1_out);
  xor XORD0_DVR (XORD0_DVR_out, out_20[0], not_1_out);
  DIVUNIT DUQ0D0d0 (
    .A(HAD0_DVD_TWOS_s), .B(XORD0_DVR_out), .Y(not_1_out), .SEL(DUQ0D0d4_EXT_c[0]), .C(DUQ0D0d0_c),
    .S(DUQ0D0d0_s));
  HA HAR0_SIGN (.A(XOR_R0_SIGN_out), .B(DVD_TWOS_EN_out), .C(HAR0_SIGN_c), .S(R[0]));
  HA HAD1_DVD_TWOS (.A(XORD1_DVD_TWOS_out), .B(HAD0_DVD_TWOS_c), .C(HAD1_DVD_TWOS_c), .S(HAD1_DVD_TWOS_s));
  xor XOR_R1_SIGN (XOR_R1_SIGN_out, DUQ0D0d1_s, DVD_TWOS_EN_out);
  Comparator #(.width(4)) comparator_1 (.a(out_16), .b(R), .eq(XR));  // open: gt, lt
  Comparator #(.width(4)) comparator_2 (.a(out_18), .b(Q), .eq(XQ));  // open: gt, lt
  xor XORD2_DVD_TWOS (XORD2_DVD_TWOS_out, out_22[2], DVD_TWOS_EN_out);
  DIVUNIT DUQ1D1d0 (
    .A(HAD1_DVD_TWOS_s), .B(XORD0_DVR_out), .Y(not_1_out), .SEL(DUQ0D0d4_EXT_c[1]), .C(DUQ1D1d0_c),
    .S(DUQ1D1d0_s));
  DIVUNIT DUQ0D0d1 (
    .A(DUQ1D1d0_s), .B(XORD1_DVR_out), .Y(DUQ0D0d0_c), .SEL(DUQ0D0d4_EXT_c[0]), .C(DUQ0D0d1_c), .S(DUQ0D0d1_s));
  HA HAR1_SIGN (.A(XOR_R1_SIGN_out), .B(HAR0_SIGN_c), .C(HAR1_SIGN_c), .S(R[1]));
  Comparator comparator_3 (.a(8'h77), .b({out_18, out_16}), .eq(comparator_3_eq));  // open: gt, lt
  Comparator comparator_4 (.a({8{1'b1}}), .b({out_18, out_16}), .eq(comparator_4_eq));  // open: gt, lt
  HA HAD2_DVD_TWOS (.A(XORD2_DVD_TWOS_out), .B(HAD1_DVD_TWOS_c), .C(HAD2_DVD_TWOS_c), .S(HAD2_DVD_TWOS_s));
  xor XOR_R2_SIGN (XOR_R2_SIGN_out, DUQ0D0d2_s, DVD_TWOS_EN_out);
  xor XORD3_DVD_TWOS (XORD3_DVD_TWOS_out, out_22[3], DVD_TWOS_EN_out);
  and and_1 (and_1_out, opsigned, comparator_3_eq);
  and and_2 (and_2_out, ~opsigned, comparator_4_eq);  // AND_Gate
  or or_1 (or_1_out, and_1_out, and_2_out);
  DIVUNIT DUQ2D2d0 (
    .A(HAD2_DVD_TWOS_s), .B(XORD0_DVR_out), .Y(not_1_out), .SEL(DUQ0D0d4_EXT_c[2]), .C(DUQ2D2d0_c),
    .S(DUQ2D2d0_s));
  DIVUNIT DUQ1D1d1 (
    .A(DUQ2D2d0_s), .B(XORD1_DVR_out), .Y(DUQ1D1d0_c), .SEL(DUQ0D0d4_EXT_c[1]), .C(DUQ1D1d1_c), .S(DUQ1D1d1_s));
  DIVUNIT DUQ0D0d2 (
    .A(DUQ1D1d1_s), .B(XORD2_DVR_out), .Y(DUQ0D0d1_c), .SEL(DUQ0D0d4_EXT_c[0]), .C(DUQ0D0d2_c), .S(DUQ0D0d2_s));
  HA HAR2_SIGN (.A(XOR_R2_SIGN_out), .B(HAR1_SIGN_c), .C(HAR2_SIGN_c), .S(R[2]));
  xnor xnor_1 (XDIV0, ediv0, or_1_out);
  HA HAD3_DVD_TWOS (.A(XORD3_DVD_TWOS_out), .B(HAD2_DVD_TWOS_c), .C(HAD3_DVD_TWOS_c), .S(HAD3_DVD_TWOS_s));
  xor XOR_R3_SIGN (XOR_R3_SIGN_out, DUQ0D0d3_s, DVD_TWOS_EN_out);
  DIVUNIT DUQ3D3d0 (
    .A(HAD3_DVD_TWOS_s), .B(XORD0_DVR_out), .Y(not_1_out), .SEL(DUQ0D0d4_EXT_c[3]), .C(DUQ3D3d0_c),
    .S(DUQ3D3d0_s));
  DIVUNIT DUQ2D2d1 (
    .A(DUQ3D3d0_s), .B(XORD1_DVR_out), .Y(DUQ2D2d0_c), .SEL(DUQ0D0d4_EXT_c[2]), .C(DUQ2D2d1_c), .S(DUQ2D2d1_s));
  DIVUNIT DUQ1D1d2 (
    .A(DUQ2D2d1_s), .B(XORD2_DVR_out), .Y(DUQ1D1d1_c), .SEL(DUQ0D0d4_EXT_c[1]), .C(DUQ1D1d2_c), .S(DUQ1D1d2_s));
  DIVUNIT DUQ0D0d3 (
    .A(DUQ1D1d2_s), .B(XORD3_DVR_out), .Y(DUQ0D0d2_c), .SEL(DUQ0D0d4_EXT_c[0]), .C(DUQ0D0d3_c), .S(DUQ0D0d3_s));
  HA HAR3_SIGN (.A(XOR_R3_SIGN_out), .B(HAR2_SIGN_c), .C(HAR3_SIGN_c), .S(R[3]));
  DIVUNIT DUQ3D3d01 (
    .A(1'b0), .B(XORD1_DVR_out), .Y(DUQ3D3d0_c), .SEL(DUQ0D0d4_EXT_c[3]), .C(DUQ3D3d01_c), .S(DUQ3D3d01_s));
  DIVUNIT DUQ2D2d2 (
    .A(DUQ3D3d01_s), .B(XORD2_DVR_out), .Y(DUQ2D2d1_c), .SEL(DUQ0D0d4_EXT_c[2]), .C(DUQ2D2d2_c),
    .S(DUQ2D2d2_s));
  DIVUNIT DUQ1D1d3 (
    .A(DUQ2D2d2_s), .B(XORD3_DVR_out), .Y(DUQ1D1d2_c), .SEL(DUQ0D0d4_EXT_c[1]), .C(DUQ1D1d3_c), .S(DUQ1D1d3_s));
  DIVUNIT DUQ0D0d4_EXT (
    .A(DUQ1D1d3_s), .B(1'b1), .Y(DUQ0D0d3_c), .SEL(DUQ0D0d4_EXT_c[0]), .C(DUQ0D0d4_EXT_c[0]),
    .S(DUQ0D0d4_EXT_s));
  xor XOR_Q0_SIGN (XOR_Q0_SIGN_out, DUQ0D0d4_EXT_c[0], QSIGN);
  DIVUNIT DUQ3D3d2 (
    .A(1'b0), .B(XORD2_DVR_out), .Y(DUQ3D3d01_c), .SEL(DUQ0D0d4_EXT_c[3]), .C(DUQ3D3d2_c), .S(DUQ3D3d2_s));
  DIVUNIT DUQ2D2d3 (
    .A(DUQ3D3d2_s), .B(XORD3_DVR_out), .Y(DUQ2D2d2_c), .SEL(DUQ0D0d4_EXT_c[2]), .C(DUQ0D0d4_EXT_c[2]),
    .S(DUQ2D2d3_s));
  DIVUNIT DUQ1D1d4_EXT (
    .A(DUQ2D2d3_s), .B(1'b1), .Y(DUQ1D1d3_c), .SEL(DUQ0D0d4_EXT_c[1]), .C(DUQ0D0d4_EXT_c[1]),
    .S(DUQ1D1d4_EXT_s));
  HA HAQ0_SIGN (.A(XOR_Q0_SIGN_out), .B(QSIGN), .C(HAQ0_SIGN_c), .S(Q[0]));
  xor XOR_Q1_SIGN (XOR_Q1_SIGN_out, DUQ0D0d4_EXT_c[1], QSIGN);
  DIVUNIT DUQ3D3d3 (
    .A(1'b0), .B(XORD3_DVR_out), .Y(DUQ3D3d2_c), .SEL(DUQ0D0d4_EXT_c[3]), .C(DUQ0D0d4_EXT_c[3]), .S(eover));
  HA HAQ1_SIGN (.A(XOR_Q1_SIGN_out), .B(HAQ0_SIGN_c), .C(HAQ1_SIGN_c), .S(Q[1]));
  xor XOR_Q2_SIGN (XOR_Q2_SIGN_out, DUQ0D0d4_EXT_c[2], QSIGN);
  HA HAQ2_SIGN (.A(XOR_Q2_SIGN_out), .B(HAQ1_SIGN_c), .C(HAQ2_SIGN_c), .S(Q[2]));
  xor XOR_Q3_SIGN (XOR_Q3_SIGN_out, DUQ0D0d4_EXT_c[3], QSIGN);
  HA HAQ3_SIGN (.A(XOR_Q3_SIGN_out), .B(HAQ2_SIGN_c), .C(HAQ3_SIGN_c), .S(Q[3]));

  assign out_17 = out_16;
  assign out_19 = out_18;
  assign out_21 = out_20;
  assign out_23 = out_22;

  // Other names for the same wires on the sheet: d_t[3:0] = out_20; D[3:0] = out_22; DIV0 = ediv0; OPSIGN = opsigned;
  //   OVER = eover

  // Notes on the sheet:
  //   opsigned: initial=0x1
  //   contents of rom_1 (hex, n*v repeats v):
  //   77 100 200 300 400 500 600 700 800 900 a00 b00 c00 d00 e00 f00 1077 1110 1201 1301 1401 1501 1601
  //   1701 1801 1901 1a01 1b01 1c01 1d01 1e01 1ff0 2077 2120 2210 2302 2402 2502 2602 2702 2802 2902 2a02
  //   2b02 2c02 2d02 2ef0 2fe0 3077 3130 3211 3310 3403 3503 3603 3703 3803 3903 3a03 3b03 3c03 3df0 3ef1
  //   3fd0 4077 4140 4220 4311 4410 4504 4604 4704 4804 4904 4a04 4b04 4cf0 4df1 4ee0 4fc0 5077 5150 5221
  //   5312 5411 5510 5605 5705 5805 5905 5a05 5bf0 5cf1 5df2 5ee1 5fb0 6077 6160 6230 6320 6412 6511 6610
  //   6706 6806 6906 6af0 6bf1 6cf2 6de0 6ed0 6fa0 7077 7170 7231 7321 7413 7512 7611 7710 7807 79f0 7af1
  //   7bf2 7cf3 7de1 7ed1 7f90 8077 8180 82c0 83ee 84e0 85fd 86fe 87ff 8810 891f 8a1e 8b1d 8c20 8d2e 8e40
  //   8f80 9077 9190 92df 93ef 94fd 95fe 96ff 97f0 9809 9910 9a1f 9b1e 9c1d 9d2f 9e3f 9f70 a077 a1a0 a2d0
  //   a3e0 a4fe a5ff a6f0 a70a a80a a90a aa10 ab1f ac1e ad20 ae30 af60 b077 b1b0 b2ef b3fe b4ff b5f0 b60b
  //   b70b b80b b90b ba0b bb10 bc1f bd1e be2f bf50 c077 c1c0 c2e0 c3ff c4f0 c50c c60c c70c c80c c90c ca0c
  //   cb0c cc10 cd1f ce20 cf40 d077 d1d0 d2ff d3f0 d40d d50d d60d d70d d80d d90d da0d db0d dc0d dd10 de1f
  //   df30 e077 e1e0 e2f0 e30e e40e e50e e60e e70e e80e e90e ea0e eb0e ec0e ed0e ee10 ef20 f077 f1f0 f20f
  //   f30f f40f f50f f60f f70f f80f f90f fa0f fb0f fc0f fd0f fe0f ff10
endmodule

module FA (
  input  A,
  input  B,
  input  Y,
  output C,
  output S
);

  wire and_1_out, and_2_out, xor_1_out;

  xor xor_1 (xor_1_out, A, B);
  and and_1 (and_1_out, B, A);
  and and_2 (and_2_out, Y, xor_1_out);
  xor xor_2 (S, xor_1_out, Y);
  or or_1 (C, and_2_out, and_1_out);
endmodule

module HA (
  input  A,
  input  B,
  output C,
  output S
);

  and and_1 (C, A, B);
  xor xor_1 (S, B, A);
endmodule

module MUXTWOS (
  input  A,
  input  B,
  output O
);

  wire multiplexer_2_out, multiplexer_3_out, not_1_out, not_2_out, not_3_out, undriven;

  not not_1 (not_1_out, A);
  Multiplexer multiplexer_1 (.in0(A), .in1(not_1_out), .out(O), .sel(B));
  not not_2 (not_2_out, undriven);
  not not_3 (not_3_out, undriven);
  not not_4 (not_3_out, undriven);
  Multiplexer multiplexer_2 (.in0(undriven), .in1(not_2_out), .out(multiplexer_2_out), .sel(not_3_out));
  Multiplexer multiplexer_3 (.in0(undriven), .in1(not_3_out), .out(multiplexer_3_out));  // open: sel
  Multiplexer multiplexer_4 (.in0(undriven), .in1(not_3_out), .out(multiplexer_3_out));  // open: sel
endmodule

module DIVUNIT (
  input  A,
  input  B,
  input  Y,
  input  SEL,
  output C,
  output S
);

  wire fa_1_s;

  FA fa_1 (.A(A), .B(B), .Y(Y), .C(C), .S(fa_1_s));
  Multiplexer multiplexer_1 (.in0(A), .in1(fa_1_s), .out(S), .sel(SEL));
endmodule
