// Logisim project DIVS6XS6.circ as structural Verilog: 5 circuits, main circuit main
module main (
  input  [5:0] dividend,
  input  D5,
  input  D4,
  input  D3,
  input  D2,
  input  D1,
  input  D0,
  input  d05,
  input  d04,
  input  d03,
  input  d02,
  input  d01,
  input  d00,
  input  [3:0] divisor,
  input  opsigned,
  input  in_16,
  output eover,
  output ediv0,
  output [5:0] quotient,
  output [5:0] remainder,
  output [5:0] out_21,
  output [5:0] out_22,
  output [5:0] out_23,
  output [5:0] out_24,
  output [5:0] out_25,
  output [5:0] out_26,
  output [5:0] out_27,
  output [5:0] out_28,
  output [5:0] out_29,
  output [5:0] out_30
);

  wire and_1_out, and_2_out, and_3_out, BREAKPOINT_out, clock_1_out, comparator_3_eq, comparator_4_eq,
       counter_1_carry, d_ff_1_q, DUQ0D0d0_c, DUQ0D0d0_s, DUQ0D0d1_c, DUQ0D0d1_s, DUQ0D0d2_c, DUQ0D0d2_s,
       DUQ0D0d3_c, DUQ0D0d3_s, DUQ0D0d4_c, DUQ0D0d4_s, DUQ0D0d5_c, DUQ0D0d5_s, DUQ0D0d6_EXT_s, DUQ1D1d0_c,
       DUQ1D1d0_s, DUQ1D1d1_c, DUQ1D1d1_s, DUQ1D1d2_c, DUQ1D1d2_s, DUQ1D1d3_c, DUQ1D1d3_s, DUQ1D1d4_c,
       DUQ1D1d4_s, DUQ1D1d5_c, DUQ1D1d5_s, DUQ1D1d6_EXT_s, DUQ2D2d0_c, DUQ2D2d0_s, DUQ2D2d1_c, DUQ2D2d1_s,
       DUQ2D2d2_c, DUQ2D2d2_s, DUQ2D2d3_c, DUQ2D2d3_s, DUQ2D2d4_c, DUQ2D2d4_s, DUQ2D2d5_c, DUQ2D2d5_s,
       DUQ2D2d6_EXT_s, DUQ3D3d0_c, DUQ3D3d0_s, DUQ3D3d01_c, DUQ3D3d01_s, DUQ3D3d2_c, DUQ3D3d2_s, DUQ3D3d3_c,
       DUQ3D3d3_s, DUQ3D3d4_c, DUQ3D3d4_s, DUQ3D3d5_c, DUQ3D3d5_s, DUQ3D3d6_EXT_s, DUQ4D4d0_c, DUQ4D4d0_s,
       DUQ4D4d1_c, DUQ4D4d1_s, DUQ4D4d2_c, DUQ4D4d2_s, DUQ4D4d3_c, DUQ4D4d3_s, DUQ4D4d4_c, DUQ4D4d4_s,
       DUQ4D4d5_s, DUQ5D5d0_c, DUQ5D5d0_s, DUQ5D5d1_c, DUQ5D5d1_s, DUQ5D5d2_c, DUQ5D5d2_s, DUQ5D5d3_c,
       DUQ5D5d3_s, DUQ5D5d4_c, DUQ5D5d4_s, DVD_TWOS_EN_out, DVR_TWOS_EN_out, HAD0_DVD_TWOS_c,
       HAD0_DVD_TWOS_s, HAD1_DVD_TWOS_c, HAD1_DVD_TWOS_s, HAD2_DVD_TWOS_c, HAD2_DVD_TWOS_s, HAD3_DVD_TWOS_c,
       HAD3_DVD_TWOS_s, HAD4_DVD_TWOS_c, HAD4_DVD_TWOS_s, HAD5_DVD_TWOS_s, HAQ0_SIGN_c, HAQ1_SIGN_c,
       HAQ2_SIGN_c, HAQ3_SIGN_c, HAQ4_SIGN_c, HAQ5_SIGN_c, HAR0_SIGN_c, HAR1_SIGN_c, HAR2_SIGN_c,
       HAR3_SIGN_c, HAR4_SIGN_c, HAR5_SIGN_c, not_1_out, or_1_out, or_2_out, QSIGN, RESET_out, XDIV0,
       XOR_Q0_SIGN_out, XOR_Q1_SIGN_out, XOR_Q2_SIGN_out, XOR_Q3_SIGN_out, XOR_Q4_SIGN_out, XOR_Q5_SIGN_out,
       XOR_R0_SIGN_out, XOR_R1_SIGN_out, XOR_R2_SIGN_out, XOR_R3_SIGN_out, XOR_R4_SIGN_out, XOR_R5_SIGN_out,
       XORD0_DVD_TWOS_out, XORD0_DVR_out, XORD1_DVD_TWOS_out, XORD1_DVR_out, XORD2_DVD_TWOS_out,
       XORD2_DVR_out, XORD3_DVD_TWOS_out, XORD3_DVR_out, XORD4_DVD_TWOS_out, XORD4_DVR_out,
       XORD5_DVD_TWOS_out, XORD5_DVR_out, XQ, XR;
  wire [5:0] DUQ0D0d6_EXT_c;
  wire [11:0] counter_1_q;

  Clock clock_1 (.out(clock_1_out));
  D_Flip_Flop d_ff_1 (.D(or_2_out), .clk(clock_1_out), .Q(d_ff_1_q), .preset(in_16));  // open: Qn, reset
  and BREAKPOINT (BREAKPOINT_out, clock_1_out, d_ff_1_q);
  xor XORD0_DVD_TWOS (XORD0_DVD_TWOS_out, out_29[0], DVD_TWOS_EN_out);
  and DVD_TWOS_EN (DVD_TWOS_EN_out, out_29[5], opsigned);
  and DVR_TWOS_EN (DVR_TWOS_EN_out, opsigned, out_27[5]);
  // Digital_Oscilloscope #(.nState(32)) digital_oscilloscope_1: pin names not known; wires that end beside it: BREAKPOINT_out, out_29[0], out_29[1], out_29[2], out_29[3], out_29[4], out_29[5], out_27[0], out_27[1], out_27[2], out_27[3]
  xor xor_1 (QSIGN, DVD_TWOS_EN_out, DVR_TWOS_EN_out);
  not not_1 (not_1_out, DVR_TWOS_EN_out);
  and DIV0ERROR (ediv0, ~out_27[5], ~out_27[4], ~out_27[3], ~out_27[2], ~out_27[1], ~out_27[0]);  // AND_Gate
  Counter #(.max('hfff), .width(12)) counter_1 (
    .clr(RESET_out), .load(1'b0), .up(1'b1), .count(1'b1), .clk(BREAKPOINT_out), .D({12{1'b0}}),
    .carry(counter_1_carry), .Q(counter_1_q));
  Button RESET (.out(RESET_out));
  HA HAD0_DVD_TWOS (.A(XORD0_DVD_TWOS_out), .B(DVD_TWOS_EN_out), .C(HAD0_DVD_TWOS_c), .S(HAD0_DVD_TWOS_s));
  xor XOR_R0_SIGN (XOR_R0_SIGN_out, DUQ0D0d0_s, DVD_TWOS_EN_out);
  xor XORD1_DVD_TWOS (XORD1_DVD_TWOS_out, out_29[1], DVD_TWOS_EN_out);
  ROM #(.addrWidth(12), .dataWidth(24)) rom_1 (.addr(counter_1_q), .data({out_29, out_27, out_25, out_21}));
  xor XORD5_DVR (XORD5_DVR_out, out_27[5], not_1_out);
  xor XORD4_DVR (XORD4_DVR_out, out_27[4], not_1_out);
  xor XORD3_DVR (XORD3_DVR_out, out_27[3], not_1_out);
  xor XORD2_DVR (XORD2_DVR_out, out_27[2], not_1_out);
  xor XORD1_DVR (XORD1_DVR_out, out_27[1], not_1_out);
  xor XORD0_DVR (XORD0_DVR_out, out_27[0], not_1_out);
  DIVUNIT DUQ0D0d0 (
    .A(HAD0_DVD_TWOS_s), .B(XORD0_DVR_out), .Y(not_1_out), .SEL(DUQ0D0d6_EXT_c[0]), .C(DUQ0D0d0_c),
    .S(DUQ0D0d0_s));
  HA HAR0_SIGN (.A(XOR_R0_SIGN_out), .B(DVD_TWOS_EN_out), .C(HAR0_SIGN_c), .S(out_23[0]));
  HA HAD1_DVD_TWOS (.A(XORD1_DVD_TWOS_out), .B(HAD0_DVD_TWOS_c), .C(HAD1_DVD_TWOS_c), .S(HAD1_DVD_TWOS_s));
  xor XOR_R1_SIGN (XOR_R1_SIGN_out, DUQ0D0d1_s, DVD_TWOS_EN_out);
  xor XORD2_DVD_TWOS (XORD2_DVD_TWOS_out, out_29[2], DVD_TWOS_EN_out);
  Comparator #(.width(6)) comparator_1 (.a(out_21), .b(out_23), .eq(XR));  // open: gt, lt
  Comparator #(.width(6)) comparator_2 (.a(out_25), .b(out_24), .eq(XQ));  // open: gt, lt
  DIVUNIT DUQ1D1d0 (
    .A(HAD1_DVD_TWOS_s), .B(XORD0_DVR_out), .Y(not_1_out), .SEL(DUQ0D0d6_EXT_c[1]), .C(DUQ1D1d0_c),
    .S(DUQ1D1d0_s));
  DIVUNIT DUQ0D0d1 (
    .A(DUQ1D1d0_s), .B(XORD1_DVR_out), .Y(DUQ0D0d0_c), .SEL(DUQ0D0d6_EXT_c[0]), .C(DUQ0D0d1_c), .S(DUQ0D0d1_s));
  HA HAR1_SIGN (.A(XOR_R1_SIGN_out), .B(HAR0_SIGN_c), .C(HAR1_SIGN_c), .S(out_23[1]));
  HA HAD2_DVD_TWOS (.A(XORD2_DVD_TWOS_out), .B(HAD1_DVD_TWOS_c), .C(HAD2_DVD_TWOS_c), .S(HAD2_DVD_TWOS_s));
  xor XOR_R2_SIGN (XOR_R2_SIGN_out, DUQ0D0d2_s, DVD_TWOS_EN_out);
  Comparator #(.width(12)) comparator_3 (.a(12'h777), .b({out_25, out_21}), .eq(comparator_3_eq));  // open: gt, lt
  Comparator #(.width(12)) comparator_4 (.a({12{1'b1}}), .b({out_25, out_21}), .eq(comparator_4_eq));  // open: gt, lt
  xor XORD3_DVD_TWOS (XORD3_DVD_TWOS_out, out_29[3], DVD_TWOS_EN_out);
  DIVUNIT DUQ2D2d0 (
    .A(HAD2_DVD_TWOS_s), .B(XORD0_DVR_out), .Y(not_1_out), .SEL(DUQ0D0d6_EXT_c[2]), .C(DUQ2D2d0_c),
    .S(DUQ2D2d0_s));
  DIVUNIT DUQ1D1d1 (
    .A(DUQ2D2d0_s), .B(XORD1_DVR_out), .Y(DUQ1D1d0_c), .SEL(DUQ0D0d6_EXT_c[1]), .C(DUQ1D1d1_c), .S(DUQ1D1d1_s));
  DIVUNIT DUQ0D0d2 (
    .A(DUQ1D1d1_s), .B(XORD2_DVR_out), .Y(DUQ0D0d1_c), .SEL(DUQ0D0d6_EXT_c[0]), .C(DUQ0D0d2_c), .S(DUQ0D0d2_s));
  HA HAR2_SIGN (.A(XOR_R2_SIGN_out), .B(HAR1_SIGN_c), .C(HAR2_SIGN_c), .S(out_23[2]));
  and and_1 (and_1_out, opsigned, comparator_3_eq);
  and and_2 (and_2_out, ~opsigned, comparator_4_eq);  // AND_Gate
  and and_3 (and_3_out, XQ, XR);
  HA HAD3_DVD_TWOS (.A(XORD3_DVD_TWOS_out), .B(HAD2_DVD_TWOS_c), .C(HAD3_DVD_TWOS_c), .S(HAD3_DVD_TWOS_s));
  or or_1 (or_1_out, and_1_out, and_2_out);
  xor XOR_R3_SIGN (XOR_R3_SIGN_out, DUQ0D0d3_s, DVD_TWOS_EN_out);
  xnor xnor_1 (XDIV0, ediv0, or_1_out);
  xor XORD4_DVD_TWOS (XORD4_DVD_TWOS_out, out_29[4], DVD_TWOS_EN_out);
  or or_2 (or_2_out, ediv0, and_3_out);
  DIVUNIT DUQ3D3d0 (
    .A(HAD3_DVD_TWOS_s), .B(XORD0_DVR_out), .Y(not_1_out), .SEL(DUQ0D0d6_EXT_c[3]), .C(DUQ3D3d0_c),
    .S(DUQ3D3d0_s));
  DIVUNIT DUQ2D2d1 (
    .A(DUQ3D3d0_s), .B(XORD1_DVR_out), .Y(DUQ2D2d0_c), .SEL(DUQ0D0d6_EXT_c[2]), .C(DUQ2D2d1_c), .S(DUQ2D2d1_s));
  DIVUNIT DUQ1D1d2 (
    .A(DUQ2D2d1_s), .B(XORD2_DVR_out), .Y(DUQ1D1d1_c), .SEL(DUQ0D0d6_EXT_c[1]), .C(DUQ1D1d2_c), .S(DUQ1D1d2_s));
  DIVUNIT DUQ0D0d3 (
    .A(DUQ1D1d2_s), .B(XORD3_DVR_out), .Y(DUQ0D0d2_c), .SEL(DUQ0D0d6_EXT_c[0]), .C(DUQ0D0d3_c), .S(DUQ0D0d3_s));
  HA HAR3_SIGN (.A(XOR_R3_SIGN_out), .B(HAR2_SIGN_c), .C(HAR3_SIGN_c), .S(out_23[3]));
  HA HAD4_DVD_TWOS (.A(XORD4_DVD_TWOS_out), .B(HAD3_DVD_TWOS_c), .C(HAD4_DVD_TWOS_c), .S(HAD4_DVD_TWOS_s));
  xor XOR_R4_SIGN (XOR_R4_SIGN_out, DUQ0D0d4_s, DVD_TWOS_EN_out);
  xor XORD5_DVD_TWOS (XORD5_DVD_TWOS_out, out_29[5], DVD_TWOS_EN_out);
  DIVUNIT DUQ4D4d0 (
    .A(HAD4_DVD_TWOS_s), .B(XORD0_DVR_out), .Y(not_1_out), .SEL(DUQ0D0d6_EXT_c[4]), .C(DUQ4D4d0_c),
    .S(DUQ4D4d0_s));
  DIVUNIT DUQ3D3d01 (
    .A(DUQ4D4d0_s), .B(XORD1_DVR_out), .Y(DUQ3D3d0_c), .SEL(DUQ0D0d6_EXT_c[3]), .C(DUQ3D3d01_c),
    .S(DUQ3D3d01_s));
  DIVUNIT DUQ2D2d2 (
    .A(DUQ3D3d01_s), .B(XORD2_DVR_out), .Y(DUQ2D2d1_c), .SEL(DUQ0D0d6_EXT_c[2]), .C(DUQ2D2d2_c),
    .S(DUQ2D2d2_s));
  DIVUNIT DUQ1D1d3 (
    .A(DUQ2D2d2_s), .B(XORD3_DVR_out), .Y(DUQ1D1d2_c), .SEL(DUQ0D0d6_EXT_c[1]), .C(DUQ1D1d3_c), .S(DUQ1D1d3_s));
  DIVUNIT DUQ0D0d4 (
    .A(DUQ1D1d3_s), .B(XORD4_DVR_out), .Y(DUQ0D0d3_c), .SEL(DUQ0D0d6_EXT_c[0]), .C(DUQ0D0d4_c), .S(DUQ0D0d4_s));
  HA HAR4_SIGN (.A(XOR_R4_SIGN_out), .B(HAR3_SIGN_c), .C(HAR4_SIGN_c), .S(out_23[4]));
  HA HAD5_DVD_TWOS (.A(XORD5_DVD_TWOS_out), .B(HAD4_DVD_TWOS_c), .S(HAD5_DVD_TWOS_s));  // open: C
  xor XOR_R5_SIGN (XOR_R5_SIGN_out, DUQ0D0d5_s, DVD_TWOS_EN_out);
  DIVUNIT DUQ5D5d0 (
    .A(HAD5_DVD_TWOS_s), .B(XORD0_DVR_out), .Y(not_1_out), .SEL(DUQ0D0d6_EXT_c[5]), .C(DUQ5D5d0_c),
    .S(DUQ5D5d0_s));
  DIVUNIT DUQ4D4d1 (
    .A(DUQ5D5d0_s), .B(XORD1_DVR_out), .Y(DUQ4D4d0_c), .SEL(DUQ0D0d6_EXT_c[4]), .C(DUQ4D4d1_c), .S(DUQ4D4d1_s));
  DIVUNIT DUQ3D3d2 (
    .A(DUQ4D4d1_s), .B(XORD2_DVR_out), .Y(DUQ3D3d01_c), .SEL(DUQ0D0d6_EXT_c[3]), .C(DUQ3D3d2_c),
    .S(DUQ3D3d2_s));
  DIVUNIT DUQ2D2d3 (
    .A(DUQ3D3d2_s), .B(XORD3_DVR_out), .Y(DUQ2D2d2_c), .SEL(DUQ0D0d6_EXT_c[2]), .C(DUQ2D2d3_c), .S(DUQ2D2d3_s));
  DIVUNIT DUQ1D1d4 (
    .A(DUQ2D2d3_s), .B(XORD4_DVR_out), .Y(DUQ1D1d3_c), .SEL(DUQ0D0d6_EXT_c[1]), .C(DUQ1D1d4_c), .S(DUQ1D1d4_s));
  DIVUNIT DUQ0D0d5 (
    .A(DUQ1D1d4_s), .B(XORD5_DVR_out), .Y(DUQ0D0d4_c), .SEL(DUQ0D0d6_EXT_c[0]), .C(DUQ0D0d5_c), .S(DUQ0D0d5_s));
  HA HAR5_SIGN (.A(XOR_R5_SIGN_out), .B(HAR4_SIGN_c), .C(HAR5_SIGN_c), .S(out_23[5]));
  DIVUNIT DUQ5D5d1 (
    .A(1'b0), .B(XORD1_DVR_out), .Y(DUQ5D5d0_c), .SEL(DUQ0D0d6_EXT_c[5]), .C(DUQ5D5d1_c), .S(DUQ5D5d1_s));
  DIVUNIT DUQ4D4d2 (
    .A(DUQ5D5d1_s), .B(XORD2_DVR_out), .Y(DUQ4D4d1_c), .SEL(DUQ0D0d6_EXT_c[4]), .C(DUQ4D4d2_c), .S(DUQ4D4d2_s));
  DIVUNIT DUQ3D3d3 (
    .A(DUQ4D4d2_s), .B(XORD3_DVR_out), .Y(DUQ3D3d2_c), .SEL(DUQ0D0d6_EXT_c[3]), .C(DUQ3D3d3_c), .S(DUQ3D3d3_s));
  DIVUNIT DUQ2D2d4 (
    .A(DUQ3D3d3_s), .B(XORD4_DVR_out), .Y(DUQ2D2d3_c), .SEL(DUQ0D0d6_EXT_c[2]), .C(DUQ2D2d4_c), .S(DUQ2D2d4_s));
  DIVUNIT DUQ1D1d5 (
    .A(DUQ2D2d4_s), .B(XORD5_DVR_out), .Y(DUQ1D1d4_c), .SEL(DUQ0D0d6_EXT_c[1]), .C(DUQ1D1d5_c), .S(DUQ1D1d5_s));
  DIVUNIT DUQ0D0d6_EXT (
    .A(DUQ1D1d5_s), .B(1'b1), .Y(DUQ0D0d5_c), .SEL(DUQ0D0d6_EXT_c[0]), .C(DUQ0D0d6_EXT_c[0]),
    .S(DUQ0D0d6_EXT_s));
  xor XOR_Q0_SIGN (XOR_Q0_SIGN_out, DUQ0D0d6_EXT_c[0], QSIGN);
  DIVUNIT DUQ5D5d2 (
    .A(1'b0), .B(XORD2_DVR_out), .Y(DUQ5D5d1_c), .SEL(DUQ0D0d6_EXT_c[5]), .C(DUQ5D5d2_c), .S(DUQ5D5d2_s));
  DIVUNIT DUQ4D4d3 (
    .A(DUQ5D5d2_s), .B(XORD3_DVR_out), .Y(DUQ4D4d2_c), .SEL(DUQ0D0d6_EXT_c[4]), .C(DUQ4D4d3_c), .S(DUQ4D4d3_s));
  DIVUNIT DUQ3D3d4 (
    .A(DUQ4D4d3_s), .B(XORD4_DVR_out), .Y(DUQ3D3d3_c), .SEL(DUQ0D0d6_EXT_c[3]), .C(DUQ3D3d4_c), .S(DUQ3D3d4_s));
  DIVUNIT DUQ2D2d5 (
    .A(DUQ3D3d4_s), .B(XORD5_DVR_out), .Y(DUQ2D2d4_c), .SEL(DUQ0D0d6_EXT_c[2]), .C(DUQ2D2d5_c), .S(DUQ2D2d5_s));
  DIVUNIT DUQ1D1d6_EXT (
    .A(DUQ2D2d5_s), .B(1'b1), .Y(DUQ1D1d5_c), .SEL(DUQ0D0d6_EXT_c[1]), .C(DUQ0D0d6_EXT_c[1]),
    .S(DUQ1D1d6_EXT_s));
  HA HAQ0_SIGN (.A(XOR_Q0_SIGN_out), .B(QSIGN), .C(HAQ0_SIGN_c), .S(out_24[0]));
  xor XOR_Q1_SIGN (XOR_Q1_SIGN_out, DUQ0D0d6_EXT_c[1], QSIGN);
  DIVUNIT DUQ5D5d3 (
    .A(1'b0), .B(XORD3_DVR_out), .Y(DUQ5D5d2_c), .SEL(DUQ0D0d6_EXT_c[5]), .C(DUQ5D5d3_c), .S(DUQ5D5d3_s));
  DIVUNIT DUQ4D4d4 (
    .A(DUQ5D5d3_s), .B(XORD4_DVR_out), .Y(DUQ4D4d3_c), .SEL(DUQ0D0d6_EXT_c[4]), .C(DUQ4D4d4_c), .S(DUQ4D4d4_s));
  DIVUNIT DUQ3D3d5 (
    .A(DUQ4D4d4_s), .B(XORD5_DVR_out), .Y(DUQ3D3d4_c), .SEL(DUQ0D0d6_EXT_c[3]), .C(DUQ3D3d5_c), .S(DUQ3D3d5_s));
  DIVUNIT DUQ2D2d6_EXT (
    .A(DUQ3D3d5_s), .B(1'b1), .Y(DUQ2D2d5_c), .SEL(DUQ0D0d6_EXT_c[2]), .C(DUQ0D0d6_EXT_c[2]),
    .S(DUQ2D2d6_EXT_s));
  HA HAQ1_SIGN (.A(XOR_Q1_SIGN_out), .B(HAQ0_SIGN_c), .C(HAQ1_SIGN_c), .S(out_24[1]));
  xor XOR_Q2_SIGN (XOR_Q2_SIGN_out, DUQ0D0d6_EXT_c[2], QSIGN);
  DIVUNIT DUQ5D5d4 (
    .A(1'b0), .B(XORD4_DVR_out), .Y(DUQ5D5d3_c), .SEL(DUQ0D0d6_EXT_c[5]), .C(DUQ5D5d4_c), .S(DUQ5D5d4_s));
  DIVUNIT DUQ4D4d5 (
    .A(DUQ5D5d4_s), .B(XORD5_DVR_out), .Y(DUQ4D4d4_c), .SEL(DUQ0D0d6_EXT_c[4]), .C(DUQ0D0d6_EXT_c[4]),
    .S(DUQ4D4d5_s));
  DIVUNIT DUQ3D3d6_EXT (
    .A(DUQ4D4d5_s), .B(1'b1), .Y(DUQ3D3d5_c), .SEL(DUQ0D0d6_EXT_c[3]), .C(DUQ0D0d6_EXT_c[3]),
    .S(DUQ3D3d6_EXT_s));
  HA HAQ2_SIGN (.A(XOR_Q2_SIGN_out), .B(HAQ1_SIGN_c), .C(HAQ2_SIGN_c), .S(out_24[2]));
  xor XOR_Q3_SIGN (XOR_Q3_SIGN_out, DUQ0D0d6_EXT_c[3], QSIGN);
  DIVUNIT DUQ5D5d5 (
    .A(1'b0), .B(XORD5_DVR_out), .Y(DUQ5D5d4_c), .SEL(DUQ0D0d6_EXT_c[5]), .C(DUQ0D0d6_EXT_c[5]), .S(eover));
  HA HAQ3_SIGN (.A(XOR_Q3_SIGN_out), .B(HAQ2_SIGN_c), .C(HAQ3_SIGN_c), .S(out_24[3]));
  xor XOR_Q4_SIGN (XOR_Q4_SIGN_out, DUQ0D0d6_EXT_c[4], QSIGN);
  HA HAQ4_SIGN (.A(XOR_Q4_SIGN_out), .B(HAQ3_SIGN_c), .C(HAQ4_SIGN_c), .S(out_24[4]));
  xor XOR_Q5_SIGN (XOR_Q5_SIGN_out, DUQ0D0d6_EXT_c[5], QSIGN);
  HA HAQ5_SIGN (.A(XOR_Q5_SIGN_out), .B(HAQ4_SIGN_c), .C(HAQ5_SIGN_c), .S(out_24[5]));

  assign out_22 = out_21;
  assign out_26 = out_25;
  assign out_28 = out_27;
  assign out_30 = out_29;
  assign quotient = out_24;
  assign remainder = out_23;

  // Other names for the same wires on the sheet: d_t[5:0] = out_27; D[5:0] = out_29; DIV0 = ediv0; OPSIGN = opsigned;
  //   OVER = eover; Q[5:0] = out_24; R[5:0] = out_23

  // Notes on the sheet:
  //   opsigned: initial=0x1
  //   contents of rom_1 (hex, n*v repeats v):
  //   7df 1000 2000 3000 4000 5000 6000 7000 8000 9000 a000 b000 c000 d000 e000 f000 10000 11000 12000
  //   13000 14000 15000 16000 17000 18000 19000 1a000 1b000 1c000 1d000 1e000 1f000 20000 21000 22000
  //   23000 24000 25000 26000 27000 28000 29000 2a000 2b000 2c000 2d000 2e000 2f000 30000 31000 32000
  //   33000 34000 35000 36000 37000 38000 39000 3a000 3b000 3c000 3d000 3e000 3f000 407df 41040 42001
  //   43001 44001 45001 46001 47001 48001 49001 4a001 4b001 4c001 4d001 4e001 4f001 50001 51001 52001
  //   53001 54001 55001 56001 57001 58001 59001 5a001 5b001 5c001 5d001 5e001 5f001 6001f 6101e 6201d
  //   6301c 6401b 6501a 66019 67018 68017 69016 6a015 6b014 6c013 6d012 6e011 6f010 7000f 7100e 7200d
  //   7300c 7400b 7500a 76009 77008 78007 79006 7a005 7b004 7c003 7d002 7e001 7ffc0 807df 81080 82040
  //   83002 84002 85002 86002 87002 88002 89002 8a002 8b002 8c002 8d002 8e002 8f002 90002 91002 92002
  //   93002 94002 95002 96002 97002 98002 99002 9a002 9b002 9c002 9d002 9e002 9f002 a001e a101d a201c
  //   a301b a401a a5019 a6018 a7017 a8016 a9015 aa014 ab013 ac012 ad011 ae010 af00f b000e b100d b200c
  //   b300b b400a b5009 b6008 b7007 b8006 b9005 ba004 bb003 bc002 bd001 befc0 bff80 c07df c10c0 c2041
  //   c3040 c4003 c5003 c6003 c7003 c8003 c9003 ca003 cb003 cc003 cd003 ce003 cf003 d0003 d1003 d2003
  //   d3003 d4003 d5003 d6003 d7003 d8003 d9003 da003 db003 dc003 dd003 de003 df003 e001d e101c e201b
  //   e301a e4019 e5018 e6017 e7016 e8015 e9014 ea013 eb012 ec011 ed010 ee00f ef00e f000d f100c f200b
  //   f300a f4009 f5008 f6007 f7006 f8005 f9004 fa003 fb002 fc001 fdfc0 fefc1 fff40 1007df 101100 102080
  //   103041 104040 105004 106004 107004 108004 109004 10a004 10b004 10c004 10d004 10e004 10f004 110004
  //   111004 112004 113004 114004 115004 116004 117004 118004 119004 11a004 11b004 11c004 11d004 11e004
  //   11f004 12001c 12101b 12201a 123019 124018 125017 126016 127015 128014 129013 12a012 12b011 12c010
  //   12d00f 12e00e 12f00d 13000c 13100b 13200a 133009 134008 135007 136006 137005 138004 139003 13a002
  //   13b001 13cfc0 13dfc2 13ef80 13ff00 1407df 141140 142081 143042 144041 145040 146005 147005 148005
  //   149005 14a005 14b005 14c005 14d005 14e005 14f005 150005 151005 152005 153005 154005 155005 156005
  //   157005 158005 159005 15a005 15b005 15c005 15d005 15e005 15f005 16001b 16101a 162019 163018 164017
  //   165016 166015 167014 168013 169012 16a011 16b010 16c00f 16d00e 16e00d 16f00c 17000b 17100a 172009
  //   173008 174007 175006 176005 177004 178003 179002 17a001 17bfc0 17cfc3 17dfc1 17ef81 17fec0 1807df
  //   181180 1820c0 183080 184042 185041 186040 187006 188006 189006 18a006 18b006 18c006 18d006 18e006
  //   18f006 190006 191006 192006 193006 194006 195006 196006 197006 198006 199006 19a006 19b006 19c006
  //   19d006 19e006 19f006 1a001a 1a1019 1a2018 1a3017 1a4016 1a5015 1a6014 1a7013 1a8012 1a9011 1aa010
  //   1ab00f 1ac00e 1ad00d 1ae00c 1af00b 1b000a 1b1009 1b2008 1b3007 1b4006 1b5005 1b6004 1b7003 1b8002
  //   1b9001 1bafc0 1bbfc4 1bcfc2 1bdf80 1bef40 1bfe80 1c07df 1c11c0 1c20c1 1c3081 1c4043 1c5042 1c6041
  //   1c7040 1c8007 1c9007 1ca007 1cb007 1cc007 1cd007 1ce007 1cf007 1d0007 1d1007 1d2007 1d3007 1d4007
  //   1d5007 1d6007 1d7007 1d8007 1d9007 1da007 1db007 1dc007 1dd007 1de007 1df007 1e0019 1e1018 1e2017
  //   1e3016 1e4015 1e5014 1e6013 1e7012 1e8011 1e9010 1ea00f 1eb00e 1ec00d 1ed00c 1ee00b 1ef00a 1f0009
  //   1f1008 1f2007 1f3006 1f4005 1f5004 1f6003 1f7002 1f8001 1f9fc0 1fafc5 1fbfc3 1fcfc1 1fdf82 1fef41
  //   1ffe40 2007df 201200 202100 203082 204080 205043 206042 207041 208040 209008 20a008 20b008 20c008
  //   20d008 20e008 20f008 210008 211008 212008 213008 214008 215008 216008 217008 218008 219008 21a008
  //   21b008 21c008 21d008 21e008 21f008 220018 221017 222016 223015 224014 225013 226012 227011 228010
  //   22900f 22a00e 22b00d 22c00c 22d00b 22e00a 22f009 230008 231007 232006 233005 234004 235003 236002
  //   237001 238fc0 239fc6 23afc4 23bfc2 23cf80 23df81 23ef00 23fe00 2407df 241240 242101 2430c0 244081
  //   245044 246043 247042 248041 249040 24a009 24b009 24c009 24d009 24e009 24f009 250009 251009 252009
  //   253009 254009 255009 256009 257009 258009 259009 25a009 25b009 25c009 25d009 25e009 25f009 260017
  //   261016 262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
endmodule

module FA (
  input  A,
  input  B,
  input  Y,
  output C,
  output S
);

  wire and_1_out, and_2_out, xor_1_out;

  xor xor_1 (xor_1_out, A, B);
  and and_1 (and_1_out, B, A);
  and and_2 (and_2_out, Y, xor_1_out);
  xor xor_2 (S, xor_1_out, Y);
  or or_1 (C, and_2_out, and_1_out);
endmodule

module HA (
  input  A,
  input  B,
  output C,
  output S
);

  and and_1 (C, A, B);
  xor xor_1 (S, B, A);
endmodule

module MUXTWOS (
  input  A,
  input  B,
  output O
);

  wire multiplexer_2_out, multiplexer_3_out, not_1_out, not_2_out, not_3_out, undriven;

  not not_1 (not_1_out, A);
  Multiplexer multiplexer_1 (.in0(A), .in1(not_1_out), .out(O), .sel(B));
  not not_2 (not_2_out, undriven);
  not not_3 (not_3_out, undriven);
  not not_4 (not_3_out, undriven);
  Multiplexer multiplexer_2 (.in0(undriven), .in1(not_2_out), .out(multiplexer_2_out), .sel(not_3_out));
  Multiplexer multiplexer_3 (.in0(undriven), .in1(not_3_out), .out(multiplexer_3_out));  // open: sel
  Multiplexer multiplexer_4 (.in0(undriven), .in1(not_3_out), .out(multiplexer_3_out));  // open: sel
endmodule

module DIVUNIT (
  input  A,
  input  B,
  input  Y,
  input  SEL,
  output C,
  output S
);

  wire fa_1_s;

  FA fa_1 (.A(A), .B(B), .Y(Y), .C(C), .S(fa_1_s));
  Multiplexer multiplexer_1 (.in0(A), .in1(fa_1_s), .out(S), .sel(SEL));
endmodule
