// Logisim project MULS4XS4.circ as structural Verilog: 4 circuits, main circuit main
module main (
  input  OP_SIGNED,
  input  A3,
  input  A2,
  input  A1,
  input  A0,
  input  B3,
  input  B2,
  input  B1,
  input  B0
);

  wire A0xB1_out, A0xB2_out, A0xB3_out, A1xB0_out, A1xB1_out, A1xB2_out, A1xB3_out, A2xB0_out, A2xB1_out,
       A2xB2_out, A2xB3_out, A3xB0_out, A3xB1_out, A3xB2_out, A3xB3_out, clock_1_out, counter_1_carry,
       FA_P2A1B1_c, FA_P2A1B1_s, FA_P3A0B3_c, FA_P3A1B2_c, FA_P3A1B2_s, FA_P3A2B1_c, FA_P3A2B1_s,
       FA_P4A1B3_c, FA_P4A2B2_c, FA_P4A2B2_s, FA_P4A3B1_c, FA_P4A3B1_s, FA_P5A2B3_c, FA_P5A3B1_EXT_c,
       FA_P5A3B1_EXT_s, FA_P5A3B2_c, FA_P5A3B2_s, FA_P6A3B1_EXT_c, FA_P6A3B1_EXT_s, FA_P6A3B2_EXT_c,
       FA_P6A3B2_EXT_s, FA_P6A3B3_c, FA_P7A3B1_EXT_s, FA_P7A3B2_EXT_s, HA_P1A0B1_c, HA_P2A0B2_c,
       P3_EXTND_EN_out, P3_INV_out, P4_EXTND_EN_out, P4_INV_out, P5_EXTND_EN_out, P5_INV_out,
       P6_EXTND_EN_out, P6_INV_out, R, RESET_out, TWOS_EN_out;
  wire [3:0] A, B;
  wire [7:0] counter_1_q, P, rom_1_data;

  Clock clock_1 (.out(clock_1_out));
  LED led_1 (.in(P[7]));
  LED led_2 (.in(P[6]));
  LED led_3 (.in(P[5]));
  LED led_4 (.in(P[4]));
  LED led_5 (.in(P[3]));
  LED led_6 (.in(P[2]));
  LED led_7 (.in(P[1]));
  LED led_8 (.in(P[0]));
  // Digital_Oscilloscope #(.nState(32)) digital_oscilloscope_1: pin names not known; wires that end beside it: clock_1_out, A[0], A[1], A[2], A[3], B[0], B[1], B[2], B[3], P[0], P[1]
  Button RESET (.out(RESET_out));
  Counter counter_1 (
    .clr(RESET_out), .load(1'b0), .up(1'b1), .count(1'b1), .clk(clock_1_out), .D({8{1'b0}}),
    .carry(counter_1_carry), .Q(counter_1_q));
  and A0xB0 (P[0], A[0], B[0]);
  ROM #(.dataWidth(16)) rom_1 (.addr(counter_1_q), .data({A, B, rom_1_data}));
  and A1xB0 (A1xB0_out, A[1], B[0]);
  and A0xB1 (A0xB1_out, A[0], B[1]);
  Comparator comparator_1 (.a(P), .b(rom_1_data), .eq(R));  // open: gt, lt
  HA HA_P1A0B1 (.A(A1xB0_out), .B(A0xB1_out), .C(HA_P1A0B1_c), .S(P[1]));
  and A2xB0 (A2xB0_out, A[2], B[0]);
  and A1xB1 (A1xB1_out, A[1], B[1]);
  and A0xB2 (A0xB2_out, A[0], B[2]);
  FA FA_P2A1B1 (.A(A2xB0_out), .B(A1xB1_out), .Y(HA_P1A0B1_c), .C(FA_P2A1B1_c), .S(FA_P2A1B1_s));
  HA HA_P2A0B2 (.A(FA_P2A1B1_s), .B(A0xB2_out), .C(HA_P2A0B2_c), .S(P[2]));
  and TWOS_EN (TWOS_EN_out, OP_SIGNED, B[3]);
  and A0xB3 (A0xB3_out, A[0], B[3]);
  and A3xB0 (A3xB0_out, A[3], B[0]);
  and A2xB1 (A2xB1_out, A[2], B[1]);
  and A1xB2 (A1xB2_out, A[1], B[2]);
  xor P3_INV (P3_INV_out, A0xB3_out, TWOS_EN_out);
  and P3_EXTND_EN (P3_EXTND_EN_out, OP_SIGNED, A3xB0_out);
  FA FA_P3A2B1 (.A(A3xB0_out), .B(A2xB1_out), .Y(FA_P2A1B1_c), .C(FA_P3A2B1_c), .S(FA_P3A2B1_s));
  FA FA_P3A1B2 (.A(FA_P3A2B1_s), .B(A1xB2_out), .Y(HA_P2A0B2_c), .C(FA_P3A1B2_c), .S(FA_P3A1B2_s));
  FA FA_P3A0B3 (.A(FA_P3A1B2_s), .B(P3_INV_out), .Y(TWOS_EN_out), .C(FA_P3A0B3_c), .S(P[3]));
  and A1xB3 (A1xB3_out, A[1], B[3]);
  and A3xB1 (A3xB1_out, A[3], B[1]);
  and A2xB2 (A2xB2_out, A[2], B[2]);
  xor P4_INV (P4_INV_out, A1xB3_out, TWOS_EN_out);
  and P4_EXTND_EN (P4_EXTND_EN_out, OP_SIGNED, A3xB1_out);
  FA FA_P4A3B1 (.A(A3xB1_out), .B(P3_EXTND_EN_out), .Y(FA_P3A2B1_c), .C(FA_P4A3B1_c), .S(FA_P4A3B1_s));
  FA FA_P4A2B2 (.A(FA_P4A3B1_s), .B(A2xB2_out), .Y(FA_P3A1B2_c), .C(FA_P4A2B2_c), .S(FA_P4A2B2_s));
  FA FA_P4A1B3 (.A(FA_P4A2B2_s), .B(P4_INV_out), .Y(FA_P3A0B3_c), .C(FA_P4A1B3_c), .S(P[4]));
  and A2xB3 (A2xB3_out, A[2], B[3]);
  and A3xB2 (A3xB2_out, A[3], B[2]);
  xor P5_INV (P5_INV_out, A2xB3_out, TWOS_EN_out);
  and P5_EXTND_EN (P5_EXTND_EN_out, OP_SIGNED, A3xB2_out);
  FA FA_P5A3B1_EXT (
    .A(P4_EXTND_EN_out), .B(FA_P4A3B1_c), .Y(P3_EXTND_EN_out), .C(FA_P5A3B1_EXT_c), .S(FA_P5A3B1_EXT_s));
  FA FA_P5A3B2 (.A(FA_P5A3B1_EXT_s), .B(A3xB2_out), .Y(FA_P4A2B2_c), .C(FA_P5A3B2_c), .S(FA_P5A3B2_s));
  FA FA_P5A2B3 (.A(FA_P5A3B2_s), .B(P5_INV_out), .Y(FA_P4A1B3_c), .C(FA_P5A2B3_c), .S(P[5]));
  and A3xB3 (A3xB3_out, A[3], B[3]);
  xor P6_INV (P6_INV_out, A3xB3_out, TWOS_EN_out);
  and P6_EXTND_EN (P6_EXTND_EN_out, OP_SIGNED, P6_INV_out);
  FA FA_P6A3B2_EXT (
    .A(FA_P6A3B1_EXT_s), .B(P5_EXTND_EN_out), .Y(FA_P5A3B2_c), .C(FA_P6A3B2_EXT_c), .S(FA_P6A3B2_EXT_s));
  FA FA_P6A3B3 (.A(FA_P6A3B2_EXT_s), .B(P6_INV_out), .Y(FA_P5A2B3_c), .C(FA_P6A3B3_c), .S(P[6]));
  FA FA_P6A3B1_EXT (
    .A(P4_EXTND_EN_out), .B(FA_P5A3B1_EXT_c), .Y(P3_EXTND_EN_out), .C(FA_P6A3B1_EXT_c), .S(FA_P6A3B1_EXT_s));
  FA FA_P7A3B1_EXT (.A(P4_EXTND_EN_out), .B(FA_P6A3B1_EXT_c), .Y(P3_EXTND_EN_out), .S(FA_P7A3B1_EXT_s));  // open: C
  FA FA_P7A3B2_EXT (.A(FA_P7A3B1_EXT_s), .B(P5_EXTND_EN_out), .Y(FA_P6A3B2_EXT_c), .S(FA_P7A3B2_EXT_s));  // open: C
  FA FA_P7A3B3_EXT (.A(FA_P7A3B2_EXT_s), .B(P6_EXTND_EN_out), .Y(FA_P6A3B3_c), .S(P[7]));  // open: C

  // Notes on the sheet:
  //   OP_SIGNED: initial=0x1
  //   contents of rom_1 (hex, n*v repeats v):
  //   0 100 200 300 400 500 600 700 800 900 a00 b00 c00 d00 e00 f00 1000 1101 1202 1303 1404 1505 1606
  //   1707 18f8 19f9 1afa 1bfb 1cfc 1dfd 1efe 1fff 2000 2102 2204 2306 2408 250a 260c 270e 28f0 29f2 2af4
  //   2bf6 2cf8 2dfa 2efc 2ffe 3000 3103 3206 3309 340c 350f 3612 3715 38e8 39eb 3aee 3bf1 3cf4 3df7 3efa
  //   3ffd 4000 4104 4208 430c 4410 4514 4618 471c 48e0 49e4 4ae8 4bec 4cf0 4df4 4ef8 4ffc 5000 5105 520a
  //   530f 5414 5519 561e 5723 58d8 59dd 5ae2 5be7 5cec 5df1 5ef6 5ffb 6000 6106 620c 6312 6418 651e 6624
  //   672a 68d0 69d6 6adc 6be2 6ce8 6dee 6ef4 6ffa 7000 7107 720e 7315 741c 7523 762a 7731 78c8 79cf 7ad6
  //   7bdd 7ce4 7deb 7ef2 7ff9 8000 81f8 82f0 83e8 84e0 85d8 86d0 87c8 8840 8938 8a30 8b28 8c20 8d18 8e10
  //   8f08 9000 91f9 92f2 93eb 94e4 95dd 96d6 97cf 9838 9931 9a2a 9b23 9c1c 9d15 9e0e 9f07 a000 a1fa a2f4
  //   a3ee a4e8 a5e2 a6dc a7d6 a830 a92a aa24 ab1e ac18 ad12 ae0c af06 b000 b1fb b2f6 b3f1 b4ec b5e7 b6e2
  //   b7dd b828 b923 ba1e bb19 bc14 bd0f be0a bf05 c000 c1fc c2f8 c3f4 c4f0 c5ec c6e8 c7e4 c820 c91c ca18
  //   cb14 cc10 cd0c ce08 cf04 d000 d1fd d2fa d3f7 d4f4 d5f1 d6ee d7eb d818 d915 da12 db0f dc0c dd09 de06
  //   df03 e000 e1fe e2fc e3fa e4f8 e5f6 e6f4 e7f2 e810 e90e ea0c eb0a ec08 ed06 ee04 ef02 f000 f1ff f2fe
  //   f3fd f4fc f5fb f6fa f7f9 f808 f907 fa06 fb05 fc04 fd03 fe02 ff01
endmodule

module FA (
  input  A,
  input  B,
  input  Y,
  output C,
  output S
);

  wire AND_AB_out, AND_Y_XOR_AB_out, XOR_AB_out;

  xor XOR_AB (XOR_AB_out, A, B);
  and AND_AB (AND_AB_out, B, A);
  and AND_Y_XOR_AB (AND_Y_XOR_AB_out, Y, XOR_AB_out);
  xor XOR_Y_XOR_AB (S, XOR_AB_out, Y);
  or OR_AND_AB_AND_Y_XOR_AB (C, AND_Y_XOR_AB_out, AND_AB_out);
endmodule

module HA (
  input  A,
  input  B,
  output C,
  output S
);

  and AND_AB (C, A, B);
  xor XOR_AB (S, B, A);
endmodule

module MUXTWOS (
  input  A,
  input  B,
  output O
);

  wire multiplexer_2_out, multiplexer_3_out, not_1_out, not_2_out, not_3_out, undriven;

  not not_1 (not_1_out, A);
  Multiplexer multiplexer_1 (.in0(A), .in1(not_1_out), .out(O), .sel(B));
  not not_2 (not_2_out, undriven);
  not not_3 (not_3_out, undriven);
  not not_4 (not_3_out, undriven);
  Multiplexer multiplexer_2 (.in0(undriven), .in1(not_2_out), .out(multiplexer_2_out), .sel(not_3_out));
  Multiplexer multiplexer_3 (.in0(undriven), .in1(not_3_out), .out(multiplexer_3_out));  // open: sel
  Multiplexer multiplexer_4 (.in0(undriven), .in1(not_3_out), .out(multiplexer_3_out));  // open: sel
endmodule
